// Logisim project 2Display.circ as structural Verilog: 3 circuits, main circuit Decoder
module Decoder (
  input  A,
  input  C,
  input  B,
  input  D,
  output Alto,
  output Centrale,
  output DX_Basso,
  output SX_basso,
  output Basso,
  output DX_alto,
  output SX_alt
);

  wire A_C_out, B_C_out, B_CD_out, C_D_out, CD_out, minus_A_B_out, minus_A_BC_out, minus_AB_out,
       minus_B_D_out, minus_C_D_out, not_1_out, not_2_out, not_3_out, not_4_out;

  not not_1 (not_1_out, B);
  not not_2 (not_2_out, A);
  and A_C (A_C_out, A, not_3_out);
  or or_1 (Alto, A_C_out, minus_B_D_out, B_CD_out, not_3_out);
  and CD (CD_out, C, D);
  or or_2 (Basso, C_D_out, minus_B_D_out, A, B_CD_out, minus_A_BC_out);
  and minus_C_D (minus_C_D_out, not_3_out, not_4_out);
  or or_3 (Centrale, A_C_out, C_D_out, B_C_out, minus_A_BC_out);
  and B_CD (B_CD_out, B, not_3_out, D);
  or or_4 (DX_alto, CD_out, A_C_out, minus_A_B_out, minus_C_D_out);
  and B_C (B_C_out, B, not_3_out);
  or or_5 (DX_Basso, D, not_3_out, minus_AB_out);
  and minus_A_BC (minus_A_BC_out, not_2_out, not_1_out, C);
  or or_6 (SX_alt, A_C_out, minus_AB_out, minus_C_D_out);
  or or_7 (SX_basso, C_D_out, minus_B_D_out);
  and minus_A_B (minus_A_B_out, not_2_out, not_1_out);
  and minus_B_D (minus_B_D_out, not_1_out, not_4_out);
  and C_D (C_D_out, C, not_4_out);
  not not_3 (not_3_out, C);
  not not_4 (not_4_out, D);
  and minus_AB (minus_AB_out, not_2_out, B);
endmodule

module Decoder2 (
  input  A,
  input  B,
  input  C,
  input  D,
  output Alto,
  output Basso,
  output Centrale,
  output DX_alto,
  output DX_Basso,
  output SX_alt,
  output SX_basso
);

  wire A_C, B_C, B_CD, C_D, CD, minus_A, minus_A_B, minus_A_BC, minus_AB, minus_B, minus_B_D, minus_C,
       minus_C_D, minus_D;

  not not_1 (minus_A, A);
  not not_2 (minus_B, B);
  not not_3 (minus_C, C);
  not not_4 (minus_D, D);
  or or_1 (Alto, A_C, C, minus_B_D, B_CD);
  or or_2 (DX_Basso, minus_C, D, minus_AB);
  and u_A_C (A_C, A, minus_C);
  and u_CD (CD, C, D);
  and u_minus_C_D (minus_C_D, minus_C, minus_D);
  or or_3 (Basso, C_D, minus_B_D, A, B_CD, minus_A_BC);
  or or_4 (SX_alt, A_C, minus_AB, minus_C_D);
  and u_B_CD (B_CD, B, minus_C, D);
  and u_B_C (B_C, B, minus_C);
  and u_minus_A_BC (minus_A_BC, minus_A, minus_B, C);
  or or_5 (Centrale, A_C, C_D, minus_A_BC, B_C);
  or or_6 (SX_basso, C_D, minus_B_D);
  and u_minus_A_B (minus_A_B, minus_A, minus_B);
  and u_minus_B_D (minus_B_D, minus_B, minus_D);
  and u_C_D (C_D, C, minus_D);
  and u_minus_AB (minus_AB, minus_A, B);
  or or_7 (DX_alto, minus_A_B, minus_C_D, CD, A_C);
endmodule

module Main (
  input  [3:0] in_1
);

  wire decoder2_1_alto, decoder2_1_basso, decoder2_1_centrale, decoder2_1_dx_alto, decoder2_1_dx_basso,
       decoder2_1_sx_alt, decoder2_1_sx_basso;

  Decoder2 decoder2_1 (
    .A(in_1[3]), .B(in_1[2]), .C(in_1[1]), .D(in_1[0]), .Alto(decoder2_1_alto),
    .DX_Basso(decoder2_1_dx_basso), .Basso(decoder2_1_basso), .SX_alt(decoder2_1_sx_alt),
    .Centrale(decoder2_1_centrale), .SX_basso(decoder2_1_sx_basso), .DX_alto(decoder2_1_dx_alto));
  _7_Segment_Display u_7_segment_display_1 (
    .g(decoder2_1_centrale), .f(decoder2_1_sx_alt), .a(decoder2_1_alto), .b(decoder2_1_dx_alto),
    .e(decoder2_1_sx_basso), .d(decoder2_1_basso), .c(decoder2_1_dx_basso));  // open: dp
endmodule
