// Logisim project ConfrontoDueNumeri2.circ as structural Verilog: 2 circuits, main circuit main
module main (
  input  A1,
  input  A0,
  input  B1,
  input  B0,
  output A_B,
  output A_B_2,
  output A_B_3
);

  Confronto confronto_1 (.A1(A1), .A0(A0), .B1(B1), .B0(B0), .E(A_B_2), .M(A_B), .m_2(A_B_3));
endmodule

module Confronto (
  input  A1,
  input  A0,
  input  B1,
  input  B0,
  output E,
  output M,
  output m_2
);

  wire nand_1_out, nand_2_out, nand_3_out, nand_4_out, nand_5_out, nand_6_out, nand_7_out, nand_8_out,
       nand_9_out, nand_10_out, nand_11_out, nand_12_out, nand_13_out, nand_14_out, nand_15_out, nand_16_out,
       nand_17_out, nand_18_out, nand_19_out, nand_20_out, nand_21_out, nand_22_out, nand_23_out, nand_24_out;

  nand nand_1 (nand_1_out, A1, A1);
  nand nand_2 (nand_2_out, A0, A0);
  nand nand_3 (nand_3_out, B1, B1);
  nand nand_4 (nand_4_out, B0, B0);
  nand nand_5 (nand_5_out, A1, A1);
  nand nand_6 (nand_6_out, B1, B1);
  nand nand_7 (nand_7_out, A0, A0);
  nand nand_8 (nand_8_out, B0, B0);
  nand nand_9 (nand_9_out, B1, B1);
  nand nand_10 (nand_10_out, B0, B0);
  nand nand_11 (nand_11_out, B1, B1);
  nand nand_12 (nand_12_out, A1, A1);
  nand nand_13 (nand_13_out, A0, A0);
  nand nand_14 (nand_14_out, A1, A1);
  nand nand_15 (nand_15_out, A0, A0);
  nand nand_16 (nand_16_out, nand_1_out, nand_2_out, nand_3_out, nand_4_out);
  nand nand_17 (nand_17_out, nand_5_out, A0, nand_6_out, B0);
  nand nand_18 (nand_18_out, A1, nand_7_out, B1, nand_8_out);
  nand nand_19 (nand_19_out, A1, A0, B1, B0);
  nand nand_20 (nand_20_out, A0, nand_9_out, nand_10_out);
  nand nand_21 (nand_21_out, A1, nand_11_out);
  nand nand_22 (nand_22_out, nand_12_out, nand_13_out, B0);
  nand nand_23 (nand_23_out, nand_14_out, B1);
  nand nand_24 (nand_24_out, nand_15_out, B1, B0);
  nand nand_25 (E, nand_16_out, nand_17_out, nand_18_out, nand_19_out);
  nand nand_26 (M, nand_20_out, nand_21_out);
  nand nand_27 (m_2, nand_22_out, nand_23_out, nand_24_out);
endmodule
