// Logisim project Display.circ as structural Verilog: 10 circuits, main circuit main
module main (
);

  wire _0, _1, _2, _3, _4, _5, _6, _7, _8, _9, a, all_1_alto, all_1_basso, all_1_centrale, all_1_dxalto,
       all_1_dxbasso, all_1_sxalto, all_1_sxbasso, b, c, d, tunnel;

  Button u__4 (.out(_4));
  Button u__8 (.out(_8));
  Button u__7 (.out(_7));
  Button u__5 (.out(_5));
  Button u__2 (.out(_2));
  Button u__1 (.out(_1));
  Button u__0 (.out(_0));
  Button u__9 (.out(_9));
  Button u__6 (.out(_6));
  Button u__3 (.out(_3));
  Button button (.out(tunnel));
  Convert convert_1 (
    .n1(_1), .n2(_2), .n3(_3), .n4(_4), .n5(_5), .n6(_6), .n7(_7), .n8(_8), .n9(_9), .n0(_0), .a(a), .b(b),
    .c(c), .d(d));
  _7_Segment_Display u_7_segment_display_1 (
    .g(all_1_centrale), .f(all_1_sxalto), .a(all_1_alto), .b(all_1_dxalto), .e(all_1_sxbasso),
    .d(all_1_basso), .c(all_1_dxbasso), .dp(tunnel));
  All all_1 (
    .a(a), .b(b), .c(c), .d(d), .Centrale(all_1_centrale), .Alto(all_1_alto), .DXalto(all_1_dxalto),
    .SXalto(all_1_sxalto), .SXbasso(all_1_sxbasso), .Basso(all_1_basso), .DXbasso(all_1_dxbasso));
endmodule

module Centrale (
  input  a,
  input  b,
  input  c,
  input  d,
  output A_2
);

  wire and_1_out, and_2_out, and_3_out, and_4_out, not_1_out, not_2_out, not_3_out, not_4_out;

  not not_1 (not_1_out, b);
  and and_1 (and_1_out, not_1_out, c);
  and and_2 (and_2_out, b, not_2_out);
  not not_2 (not_2_out, c);
  and and_3 (and_3_out, b, not_3_out);
  not not_3 (not_3_out, d);
  and and_4 (and_4_out, a, not_4_out);
  not not_4 (not_4_out, b);
  or or_1 (A_2, and_1_out, and_2_out, and_3_out, and_4_out);
endmodule

module Basso (
  input  a,
  input  b,
  input  c,
  input  d,
  output A_2
);

  wire and_1_out, and_2_out, and_3_out, and_4_out, and_5_out, not_1_out, not_2_out, not_3_out, not_4_out,
       not_5_out, not_6_out, not_7_out, not_8_out, not_9_out;

  not not_1 (not_1_out, b);
  not not_2 (not_2_out, d);
  not not_3 (not_3_out, a);
  not not_4 (not_4_out, b);
  not not_5 (not_5_out, d);
  not not_6 (not_6_out, a);
  not not_7 (not_7_out, c);
  not not_8 (not_8_out, b);
  not not_9 (not_9_out, c);
  and and_1 (and_1_out, not_1_out, not_2_out);
  and and_2 (and_2_out, not_3_out, not_4_out, c);
  and and_3 (and_3_out, c, not_5_out);
  and and_4 (and_4_out, not_6_out, b, not_7_out, d);
  and and_5 (and_5_out, a, not_8_out, not_9_out);
  or or_1 (A_2, and_1_out, and_2_out, and_3_out, and_4_out, and_5_out);
endmodule

module Alto (
  input  a,
  input  b,
  input  c,
  input  d,
  output a2
);

  wire and_1_out, and_2_out, and_3_out, and_4_out, and_5_out, and_6_out, not_1_out, not_2_out, not_3_out,
       not_4_out, not_5_out, not_6_out, not_7_out;

  not not_1 (not_1_out, b);
  and and_1 (and_1_out, not_1_out, not_2_out);
  not not_2 (not_2_out, d);
  not not_3 (not_3_out, a);
  and and_2 (and_2_out, not_3_out, c);
  not not_4 (not_4_out, a);
  and and_3 (and_3_out, not_4_out, b, d);
  and and_4 (and_4_out, a, not_5_out);
  not not_5 (not_5_out, b);
  and and_5 (and_5_out, a, not_6_out);
  not not_6 (not_6_out, c);
  and and_6 (and_6_out, a, not_7_out);
  not not_7 (not_7_out, d);
  or or_1 (a2, and_1_out, and_2_out, and_3_out, and_4_out, and_5_out, and_6_out);
endmodule

module DXalto (
  input  a,
  input  b,
  input  c,
  input  d,
  output A_2
);

  wire and_1_out, and_2_out, not_1_out, not_2_out, not_3_out, not_4_out;

  not not_1 (not_1_out, b);
  not not_2 (not_2_out, c);
  and and_1 (and_1_out, not_2_out, not_3_out);
  not not_3 (not_3_out, d);
  not not_4 (not_4_out, a);
  and and_2 (and_2_out, not_4_out, c, d);
  or or_1 (A_2, not_1_out, and_1_out, and_2_out);
endmodule

module SXalto (
  input  a,
  input  b,
  input  c,
  input  d,
  output A_2
);

  wire and_1_out, and_2_out, and_3_out, and_4_out, not_1_out, not_2_out, not_3_out, not_4_out, not_5_out;

  not not_1 (not_1_out, c);
  and and_1 (and_1_out, not_1_out, not_2_out);
  not not_2 (not_2_out, d);
  and and_2 (and_2_out, b, not_3_out);
  not not_3 (not_3_out, c);
  and and_3 (and_3_out, b, not_4_out);
  not not_4 (not_4_out, d);
  and and_4 (and_4_out, a, not_5_out);
  not not_5 (not_5_out, b);
  or or_1 (A_2, and_1_out, and_2_out, and_3_out, and_4_out);
endmodule

module SXbasso (
  input  a,
  input  b,
  input  c,
  input  d,
  output A_2
);

  wire and_1_out, and_2_out, and_3_out, and_4_out, not_1_out, not_2_out, not_3_out, not_4_out, not_5_out;

  not not_1 (not_1_out, b);
  and and_1 (and_1_out, not_1_out, not_2_out);
  not not_2 (not_2_out, d);
  and and_2 (and_2_out, c, not_3_out);
  not not_3 (not_3_out, d);
  and and_3 (and_3_out, a, not_4_out, c);
  not not_4 (not_4_out, b);
  and and_4 (and_4_out, a, b, not_5_out);
  not not_5 (not_5_out, c);
  or or_1 (A_2, and_1_out, and_2_out, and_3_out, and_4_out);
endmodule

module DXbasso (
  input  a,
  input  b,
  input  c,
  input  d,
  output A_2
);

  wire and_1_out, and_2_out, and_3_out, not_1_out, not_2_out, not_3_out, not_4_out;

  not not_1 (not_1_out, c);
  not not_2 (not_2_out, b);
  and and_1 (and_1_out, not_2_out, d);
  not not_3 (not_3_out, a);
  and and_2 (and_2_out, not_3_out, b);
  and and_3 (and_3_out, b, not_4_out);
  not not_4 (not_4_out, d);
  or or_1 (A_2, not_1_out, and_1_out, and_2_out, and_3_out);
endmodule

module All (
  input  a,
  input  b,
  input  c,
  input  d,
  output Centrale,
  output Alto,
  output DXalto,
  output SXalto,
  output SXbasso,
  output Basso,
  output DXbasso
);

  Centrale centrale_1 (.a(a), .b(b), .c(c), .d(d), .A_2(Centrale));
  Alto alto_1 (.a(a), .b(b), .c(c), .d(d), .a2(Alto));
  DXalto dxalto_1 (.a(a), .b(b), .c(c), .d(d), .A_2(DXalto));
  SXalto sxalto_1 (.a(a), .b(b), .c(c), .d(d), .A_2(SXalto));
  SXbasso sxbasso_1 (.a(a), .b(b), .c(c), .d(d), .A_2(SXbasso));
  Basso basso_1 (.a(a), .b(b), .c(c), .d(d), .A_2(Basso));
  DXbasso dxbasso_1 (.a(a), .b(b), .c(c), .d(d), .A_2(DXbasso));
endmodule

module Convert (
  input  n1,
  input  n2,
  input  n3,
  input  n4,
  input  n5,
  input  n6,
  input  n7,
  input  n8,
  input  n9,
  input  n0,
  output a,
  output b,
  output c,
  output d
);

  wire not_1_out, not_2_out, not_3_out, not_4_out, not_5_out, not_6_out, not_7_out, not_8_out, not_9_out,
       not_10_out, not_11_out, not_12_out, not_13_out, not_14_out, not_15_out, not_16_out, not_17_out,
       not_18_out, not_19_out, not_20_out, not_21_out, not_22_out, not_23_out, not_24_out, not_25_out;

  not not_1 (not_1_out, n1);
  not not_2 (not_2_out, n2);
  not not_3 (not_3_out, n3);
  not not_4 (not_4_out, n4);
  not not_5 (not_5_out, n5);
  not not_6 (not_6_out, n6);
  not not_7 (not_7_out, n7);
  not not_8 (not_8_out, n0);
  not not_9 (not_9_out, n1);
  not not_10 (not_10_out, n2);
  not not_11 (not_11_out, n3);
  not not_12 (not_12_out, n8);
  not not_13 (not_13_out, n9);
  not not_14 (not_14_out, n0);
  not not_15 (not_15_out, n1);
  not not_16 (not_16_out, n4);
  not not_17 (not_17_out, n5);
  not not_18 (not_18_out, n8);
  not not_19 (not_19_out, n9);
  not not_20 (not_20_out, n0);
  not not_21 (not_21_out, n2);
  not not_22 (not_22_out, n4);
  not not_23 (not_23_out, n6);
  not not_24 (not_24_out, n8);
  not not_25 (not_25_out, n0);
  and and_1 (a, not_1_out, not_2_out, not_3_out, not_4_out, not_5_out, not_6_out, not_7_out, not_8_out);
  and and_2 (b, not_9_out, not_10_out, not_11_out, not_12_out, not_13_out, not_14_out);
  and and_3 (c, not_15_out, not_16_out, not_17_out, not_18_out, not_19_out, not_20_out);
  and and_4 (d, not_21_out, not_22_out, not_23_out, not_24_out, not_25_out);
endmodule
