// Logisim project 2to4 Decoder.circ as structural Verilog: 1 circuit, main circuit main
module main (
  input  A,
  input  [1:0] BC,
  output out_3
);

  wire decoder_1_out0, decoder_1_out1, decoder_2_out0, decoder_2_out2, decoder_2_out3, not_1_out;

  Decoder #(.select(2)) decoder_1 (
    .out0(decoder_1_out0), .out1(decoder_1_out1), .sel(BC), .en(not_1_out));  // open: out2, out3
  not not_1 (not_1_out, A);
  Decoder #(.select(2)) decoder_2 (
    .out0(decoder_2_out0), .out2(decoder_2_out2), .out3(decoder_2_out3), .sel(BC), .en(A));  // open: out1
  or or_1 (out_3, decoder_1_out0, decoder_1_out1, decoder_2_out0, decoder_2_out2, decoder_2_out3);

  // Notes on the sheet:
  //   F(A,B,C)=SUMm(0,1,4,6,7)
endmodule
