// Logisim project AdderConMultiplex.circ as structural Verilog: 1 circuit, main circuit main
module main (
  input  [2:0] in_1,
  output S,
  output Cout
);

  wire and_1_out, decoder_1_out1, decoder_1_out2, decoder_1_out3, decoder_1_out4, decoder_1_out5,
       decoder_1_out6, decoder_1_out7, not_1_out, not_2_out, or_1_out, xnor_1_out, xor_1_out;

  not not_1 (not_1_out, in_1[0]);
  Decoder #(.select(3)) decoder_1 (
    .out1(decoder_1_out1), .out2(decoder_1_out2), .out3(decoder_1_out3), .out4(decoder_1_out4),
    .out5(decoder_1_out5), .out6(decoder_1_out6), .out7(decoder_1_out7), .sel(in_1));  // open: out0, en
  Multiplexer #(.select(2)) multiplexer_1 (
    .in0(in_1[0]), .in1(not_1_out), .in2(not_1_out), .in3(in_1[0]), .out(S), .sel(in_1[2:1]));  // open: en
  xor xor_1 (xor_1_out, in_1[1], in_1[0]);
  xnor xnor_1 (xnor_1_out, in_1[0], in_1[1]);
  Multiplexer multiplexer_2 (.in0(xor_1_out), .in1(xnor_1_out), .out(S), .sel(in_1[2]));  // open: en
  or u_S (S, decoder_1_out1, decoder_1_out2, decoder_1_out4, decoder_1_out7);
  or Cin (Cout, decoder_1_out3, decoder_1_out5, decoder_1_out6, decoder_1_out7);
  not not_2 (not_2_out, 1'b1);
  Multiplexer #(.select(2)) multiplexer_3 (
    .in0(not_2_out), .in1(in_1[0]), .in2(in_1[0]), .in3(1'b1), .out(Cout), .sel(in_1[2:1]));  // open: en
  and and_1 (and_1_out, in_1[1], in_1[0]);
  or or_1 (or_1_out, in_1[0], in_1[1]);
  Multiplexer multiplexer_4 (.in0(and_1_out), .in1(or_1_out), .out(Cout), .sel(in_1[2]));  // open: en

  // Notes on the sheet:
  //   Adder con 3t08 decoder
  //   Adder con 1to2 Multiplex
  //   Adder con 2to4 Multiplex
endmodule
