// Logisim project 01.circ as structural Verilog: 2 circuits, main circuit main
module main (
  input  A,
  input  B,
  input  C,
  input  X,
  output Da,
  output Db,
  output Dc,
  output Z
);

  wire and_1_out, and_2_out, and_3_out, and_4_out, and_5_out, and_6_out, and_7_out, and_8_out, and_9_out,
       and_10_out, and_11_out, not_1_out, not_2_out, not_3_out, not_4_out, not_5_out, not_6_out, not_7_out,
       not_8_out, not_9_out, not_10_out, not_11_out, not_12_out, not_13_out, not_14_out, not_15_out,
       not_16_out;

  and and_1 (and_1_out, B, not_1_out, not_2_out);
  not not_1 (not_1_out, C);
  not not_2 (not_2_out, X);
  and and_2 (and_2_out, B, C, X);
  not not_3 (not_3_out, A);
  and and_3 (and_3_out, not_3_out, not_4_out, C);
  not not_4 (not_4_out, B);
  not not_5 (not_5_out, A);
  and and_4 (and_4_out, not_5_out, C, not_6_out);
  not not_6 (not_6_out, X);
  not not_7 (not_7_out, B);
  and and_5 (and_5_out, not_7_out, C, not_8_out);
  not not_8 (not_8_out, X);
  and and_6 (and_6_out, A, B, not_9_out);
  not not_9 (not_9_out, C);
  and and_7 (and_7_out, A, B, X);
  not not_10 (not_10_out, A);
  and and_8 (and_8_out, not_10_out, not_11_out, X);
  not not_11 (not_11_out, B);
  not not_12 (not_12_out, A);
  not not_13 (not_13_out, C);
  and and_9 (and_9_out, not_12_out, not_13_out, X);
  not not_14 (not_14_out, C);
  and and_10 (and_10_out, A, not_14_out, not_15_out);
  not not_15 (not_15_out, X);
  and and_11 (and_11_out, A, C, X);
  not not_16 (not_16_out, X);
  or or_1 (Da, and_1_out, and_2_out, A);
  or or_2 (Db, and_3_out, and_4_out, and_5_out, and_6_out, and_7_out);
  or or_3 (Dc, and_8_out, and_9_out, and_10_out, and_11_out);
  and and_12 (Z, A, B, C, not_16_out);
endmodule

module fgf (
  input  in_1,
  output out_2
);

  wire clock_1_out, d_ff_1_q, d_ff_2_q, d_ff_3_q, main_1_da, main_1_db, main_1_dc;

  Clock clock_1 (.out(clock_1_out));
  D_Flip_Flop d_ff_1 (.clk(clock_1_out), .D(main_1_da), .Q(d_ff_1_q));  // open: Qn, preset, en, reset
  D_Flip_Flop d_ff_2 (.clk(clock_1_out), .D(main_1_db), .Q(d_ff_2_q));  // open: Qn, preset, en, reset
  main main_1 (
    .A(d_ff_1_q), .B(d_ff_2_q), .C(d_ff_3_q), .X(in_1), .Da(main_1_da), .Db(main_1_db), .Dc(main_1_dc),
    .Z(out_2));
  D_Flip_Flop d_ff_3 (.clk(clock_1_out), .D(main_1_dc), .Q(d_ff_3_q));  // open: Qn, preset, en, reset

  // Notes on the sheet:
  //   A
  //   B
  //   C
endmodule
