// Logisim project C29M05E01A.circ as structural Verilog: 3 circuits, main circuit main
module main (
  input  A,
  input  B,
  input  C,
  input  X,
  output Ta,
  output Tb,
  output Tc
);

  wire and_1_out, and_2_out, and_3_out, and_4_out, and_5_out, and_6_out, and_7_out, and_8_out, and_9_out,
       and_10_out, not_1_out, not_2_out, not_3_out, not_4_out, not_5_out, not_6_out, not_7_out, not_8_out;

  and and_1 (and_1_out, B, C, X);
  and and_2 (and_2_out, A, C, X);
  and and_3 (and_3_out, A, B);
  not not_1 (not_1_out, A);
  not not_2 (not_2_out, B);
  not not_3 (not_3_out, X);
  not not_4 (not_4_out, C);
  not not_5 (not_5_out, A);
  not not_6 (not_6_out, B);
  not not_7 (not_7_out, X);
  not not_8 (not_8_out, C);
  or or_1 (Ta, and_1_out, and_2_out, and_3_out);
  and and_4 (and_4_out, not_1_out, not_2_out, C, not_3_out);
  or or_2 (Tb, and_4_out, and_5_out, and_6_out);
  and and_5 (and_5_out, B, C, X);
  and and_6 (and_6_out, A, C, X);
  and and_7 (and_7_out, not_4_out, X);
  and and_8 (and_8_out, not_5_out, not_6_out, C, not_7_out);
  and and_9 (and_9_out, B, not_8_out);
  and and_10 (and_10_out, B, X);
  or or_3 (Tc, and_7_out, and_8_out, and_9_out, and_10_out);
endmodule

module ffghf (
  input  in_1
);

  wire clock_1_out, main_1_ta, main_1_tb, main_1_tc, t_ff_1_q, t_ff_2_q, t_ff_3_q;

  Clock clock_1 (.out(clock_1_out));
  T_Flip_Flop t_ff_1 (.clk(clock_1_out), .T(main_1_ta), .Q(t_ff_1_q));  // open: Qn, preset, reset, en
  T_Flip_Flop t_ff_2 (.clk(clock_1_out), .T(main_1_tb), .Q(t_ff_2_q));  // open: Qn, preset, reset, en
  main main_1 (.A(t_ff_1_q), .B(t_ff_2_q), .C(t_ff_3_q), .X(in_1), .Ta(main_1_ta), .Tb(main_1_tb), .Tc(main_1_tc));
  T_Flip_Flop t_ff_3 (.clk(clock_1_out), .T(main_1_tc), .Q(t_ff_3_q));  // open: Qn, preset, reset, en

  // Notes on the sheet:
  //   A
  //   B
  //   C
endmodule

module hfh (
  input  A,
  input  B,
  input  C,
  input  D,
  output F
);

  wire and_1_out, and_2_out, and_3_out, and_4_out, not_1_out, not_2_out, not_3_out, not_4_out, not_5_out;

  not not_1 (not_1_out, B);
  and and_1 (and_1_out, not_1_out, not_2_out);
  not not_2 (not_2_out, C);
  not not_3 (not_3_out, C);
  and and_2 (and_2_out, not_3_out, D);
  not not_4 (not_4_out, A);
  and and_3 (and_3_out, not_4_out, B, C);
  and and_4 (and_4_out, A, not_5_out);
  not not_5 (not_5_out, B);
  or or_1 (F, and_1_out, and_2_out, and_3_out, and_4_out);
endmodule
