// Logisim project Counter.circ as structural Verilog: 5 circuits, main circuit main
module main (
);

  wire clock_1_out, counter_1_a, counter_1_b, counter_1_c, counter_1_d, decoder_1_alto, decoder_1_basso,
       decoder_1_centrale, decoder_1_dx_alto, decoder_1_dx_basso, decoder_1_sx_alt, decoder_1_sx_basso;

  Clock clock_1 (.out(clock_1_out));
  Counter counter_1 (.in_1(clock_1_out), .A(counter_1_a), .B(counter_1_b), .C(counter_1_c), .D(counter_1_d));
  Decoder decoder_1 (
    .A(counter_1_a), .B(counter_1_b), .C(counter_1_c), .D(counter_1_d), .Alto(decoder_1_alto),
    .DX_Basso(decoder_1_dx_basso), .Basso(decoder_1_basso), .SX_alt(decoder_1_sx_alt),
    .Centrale(decoder_1_centrale), .SX_basso(decoder_1_sx_basso), .DX_alto(decoder_1_dx_alto));
  _7_Segment_Display u_7_segment_display_1 (
    .g(decoder_1_centrale), .f(decoder_1_sx_alt), .a(decoder_1_alto), .b(decoder_1_dx_alto),
    .e(decoder_1_sx_basso), .d(decoder_1_basso), .c(decoder_1_dx_basso));  // open: dp
endmodule

module Decoder (
  input  A,
  input  B,
  input  C,
  input  D,
  output Alto,
  output Basso,
  output Centrale,
  output DX_alto,
  output DX_Basso,
  output SX_alt,
  output SX_basso
);

  wire A_C, B_C, B_CD, C_D, CD, minus_A, minus_A_B, minus_A_BC, minus_AB, minus_B, minus_B_D, minus_C,
       minus_C_D, minus_D;

  not not_1 (minus_A, A);
  not not_2 (minus_B, B);
  not not_3 (minus_C, C);
  not not_4 (minus_D, D);
  or or_1 (Alto, A_C, C, minus_B_D, B_CD);
  or or_2 (DX_Basso, minus_C, D, minus_AB);
  and u_A_C (A_C, A, minus_C);
  and u_CD (CD, C, D);
  and u_minus_C_D (minus_C_D, minus_C, minus_D);
  or or_3 (Basso, C_D, minus_B_D, A, B_CD, minus_A_BC);
  or or_4 (SX_alt, A_C, minus_AB, minus_C_D);
  and u_B_CD (B_CD, B, minus_C, D);
  and u_B_C (B_C, B, minus_C);
  and u_minus_A_BC (minus_A_BC, minus_A, minus_B, C);
  or or_5 (Centrale, A_C, C_D, minus_A_BC, B_C);
  or or_6 (SX_basso, C_D, minus_B_D);
  and u_minus_A_B (minus_A_B, minus_A, minus_B);
  and u_minus_B_D (minus_B_D, minus_B, minus_D);
  and u_C_D (C_D, C, minus_D);
  and u_minus_AB (minus_AB, minus_A, B);
  or or_7 (DX_alto, minus_A_B, minus_C_D, CD, A_C);
endmodule

module Counter (
  input  in_1,
  output A,
  output B,
  output C,
  output D
);

  wire and_1_out, and_2_out, and_3_out, and_4_out, not_1_out, t_ff_1_q;

  T_Flip_Flop t_ff_1 (.clk(in_1), .T(and_4_out), .Q(t_ff_1_q), .reset(t_ff_1_q));  // open: Qn, preset, en
  T_Flip_Flop t_ff_2 (.clk(in_1), .T(and_1_out), .Q(A), .reset(t_ff_1_q));  // open: Qn, preset, en
  and and_1 (and_1_out, D, C, B);
  T_Flip_Flop t_ff_3 (.clk(in_1), .T(and_2_out), .Q(B), .reset(t_ff_1_q));  // open: Qn, preset, en
  and and_2 (and_2_out, D, C);
  T_Flip_Flop t_ff_4 (.clk(in_1), .T(and_3_out), .Q(C), .reset(t_ff_1_q));  // open: Qn, preset, en
  not not_1 (not_1_out, A);
  and and_3 (and_3_out, not_1_out, D);
  T_Flip_Flop t_ff_5 (.clk(in_1), .T(1'b1), .Q(D), .reset(t_ff_1_q));  // open: Qn, preset, en
  and and_4 (and_4_out, D, A);
endmodule

module Counter_Gary (
  output A,
  output B,
  output C
);

  wire and_1_out, and_2_out, and_3_out, and_4_out, and_5_out, and_6_out, and_7_out, and_8_out, clock_1_out,
       not_1_out, not_2_out, not_3_out, not_4_out, not_5_out, not_6_out, not_7_out, not_8_out, not_9_out,
       not_10_out, not_11_out, not_12_out, or_1_out, or_2_out, t_ff_1_q;

  Clock clock_1 (.out(clock_1_out));
  T_Flip_Flop t_ff_1 (.clk(clock_1_out), .T(and_8_out), .Q(t_ff_1_q), .reset(t_ff_1_q));  // open: Qn, preset, en
  and and_1 (and_1_out, not_1_out, B, not_2_out);
  or or_1 (or_1_out, and_2_out, and_3_out);
  or or_2 (or_2_out, and_4_out, and_5_out, and_6_out, and_7_out);
  T_Flip_Flop t_ff_2 (.clk(clock_1_out), .T(and_1_out), .Q(A), .reset(t_ff_1_q));  // open: Qn, preset, en
  not not_1 (not_1_out, A);
  not not_2 (not_2_out, C);
  T_Flip_Flop t_ff_3 (.clk(clock_1_out), .T(or_1_out), .Q(B), .reset(t_ff_1_q));  // open: Qn, preset, en
  not not_3 (not_3_out, A);
  and and_2 (and_2_out, not_3_out, C, not_4_out);
  not not_4 (not_4_out, B);
  and and_3 (and_3_out, A, B, C);
  T_Flip_Flop t_ff_4 (.clk(clock_1_out), .T(or_2_out), .Q(C), .reset(t_ff_1_q));  // open: Qn, preset, en
  and and_4 (and_4_out, not_5_out, not_6_out, not_7_out);
  and and_5 (and_5_out, not_8_out, B, C);
  and and_6 (and_6_out, A, B, not_9_out);
  not not_5 (not_5_out, A);
  not not_6 (not_6_out, B);
  not not_7 (not_7_out, C);
  not not_8 (not_8_out, A);
  not not_9 (not_9_out, C);
  and and_7 (and_7_out, A, not_10_out, C);
  not not_10 (not_10_out, B);
  not not_11 (not_11_out, B);
  and and_8 (and_8_out, A, not_11_out, not_12_out);
  not not_12 (not_12_out, C);
endmodule

module Gary_D (
  output A,
  output B,
  output C
);

  wire and_1_out, and_2_out, and_3_out, and_4_out, and_5_out, and_6_out, and_7_out, clock_1_out, d_ff_1_q,
       not_1_out, not_2_out, not_3_out, not_4_out, not_5_out, not_6_out, not_7_out, or_1_out, or_2_out,
       or_3_out;

  Clock clock_1 (.out(clock_1_out));
  D_Flip_Flop d_ff_1 (.clk(clock_1_out), .D(and_1_out), .Q(d_ff_1_q), .reset(d_ff_1_q));  // open: Qn, preset, en
  not not_1 (not_1_out, B);
  and and_1 (and_1_out, A, not_1_out, not_2_out);
  not not_2 (not_2_out, C);
  or or_1 (or_1_out, and_2_out, and_3_out);
  or or_2 (or_2_out, and_4_out, and_5_out);
  or or_3 (or_3_out, and_6_out, and_7_out);
  and and_2 (and_2_out, not_6_out, not_7_out);
  and and_3 (and_3_out, A, B);
  D_Flip_Flop d_ff_2 (.clk(clock_1_out), .D(or_2_out), .Q(A), .reset(d_ff_1_q));  // open: Qn, preset, en
  and and_4 (and_4_out, B, not_3_out);
  not not_3 (not_3_out, C);
  and and_5 (and_5_out, C, A);
  D_Flip_Flop d_ff_3 (.clk(clock_1_out), .D(or_3_out), .Q(B), .reset(d_ff_1_q));  // open: Qn, preset, en
  not not_4 (not_4_out, A);
  and and_6 (and_6_out, not_4_out, C);
  and and_7 (and_7_out, B, not_5_out);
  not not_5 (not_5_out, C);
  D_Flip_Flop d_ff_4 (.clk(clock_1_out), .D(or_1_out), .Q(C), .reset(d_ff_1_q));  // open: Qn, preset, en
  not not_6 (not_6_out, A);
  not not_7 (not_7_out, B);
endmodule
