// Logisim project Encoder.circ as structural Verilog: 2 circuits, main circuit main
module main (
  input  in_1,
  input  in_2,
  input  in_3,
  input  in_4,
  input  in_5,
  input  in_6,
  input  in_7,
  output [3:0] out_8
);

  wire _0, _1, _2, _3, _4, _5, _6, _7, _8, _9, encoder_1_a, encoder_1_b, encoder_1_c, encoder_1_d,
       encoder_2_a, encoder_2_b, encoder_2_c, not_1_out;

  Button u__8 (.out(_8));
  Button u__7 (.out(_7));
  Button u__4 (.out(_4));
  Button u__5 (.out(_5));
  Button u__1 (.out(_1));
  Button u__0 (.out(_0));
  Button u__9 (.out(_9));
  Button u__6 (.out(_6));
  Button u__3 (.out(_3));
  Button u__2 (.out(_2));
  Encoder encoder_1 (
    .n0(_0), .n1(_1), .n2(_2), .n3(_3), .n4(_4), .n5(_5), .n6(_6), .n7(_7), .in_9(in_1), .A(encoder_1_a),
    .B(encoder_1_b), .C(encoder_1_c), .d(encoder_1_d));
  not not_1 (not_1_out, encoder_1_d);
  Encoder encoder_2 (
    .n0(_8), .n1(_9), .n2(in_2), .n3(in_3), .n4(in_4), .n5(in_5), .n6(in_6), .n7(in_7), .in_9(not_1_out),
    .A(encoder_2_a), .B(encoder_2_b), .C(encoder_2_c), .d(out_8[3]));
  or or_1 (out_8[2], encoder_1_a, encoder_2_a);
  or or_2 (out_8[1], encoder_1_b, encoder_2_b);
  or or_3 (out_8[0], encoder_1_c, encoder_2_c);
endmodule

module Encoder (
  input  n0,
  input  n1,
  input  n2,
  input  n3,
  input  n4,
  input  n5,
  input  n6,
  input  n7,
  input  in_9,
  output A,
  output B,
  output C,
  output d
);

  wire and_1_out, and_2_out, and_4_out, and_5_out, and_6_out, and_7_out, and_8_out, not_1_out, not_2_out,
       not_3_out, not_4_out, not_5_out, not_6_out, or_1_out;

  not not_1 (not_1_out, n6);
  not not_2 (not_2_out, n7);
  or or_1 (or_1_out, n7, n6, n5, n4, n3, n2, n1, n0);
  not not_3 (not_3_out, n5);
  and and_1 (and_1_out, n6, not_2_out, in_9);
  and and_2 (and_2_out, n7, in_9);
  and and_3 (d, or_1_out, in_9);
  not not_4 (not_4_out, n3);
  not not_5 (not_5_out, n4);
  and and_4 (and_4_out, n4, not_1_out, not_2_out, not_3_out, in_9);
  and and_5 (and_5_out, n5, not_2_out, not_1_out, in_9);
  not not_6 (not_6_out, n2);
  and and_6 (and_6_out, n3, not_5_out, not_3_out, not_1_out, not_2_out, in_9);
  and and_7 (and_7_out, n2, not_1_out, not_4_out, not_2_out, not_3_out, not_5_out, in_9);
  and and_8 (and_8_out, n1, not_4_out, not_1_out, not_6_out, not_2_out, not_3_out, not_5_out, in_9);
  or or_2 (A, and_4_out, and_5_out, and_1_out, and_2_out);
  or or_3 (B, and_6_out, and_7_out, and_1_out, and_2_out);
  or or_4 (C, and_2_out, and_5_out, and_6_out, and_8_out);
endmodule
