// Logisim project L11P47.circ as structural Verilog: 2 circuits, main circuit main
module main (
  output A,
  output B,
  output C
);

  wire and_1_out, and_2_out, and_3_out, and_4_out, and_5_out, and_6_out, and_7_out, and_8_out, clock_1_out,
       not_1_out, not_2_out, not_3_out, not_4_out, not_5_out, not_6_out, not_7_out, not_8_out, not_9_out,
       not_10_out, not_11_out, not_12_out, or_1_out, or_2_out, t_ff_1_q;

  Clock clock_1 (.out(clock_1_out));
  T_Flip_Flop t_ff_1 (.clk(clock_1_out), .T(and_8_out), .Q(t_ff_1_q), .reset(t_ff_1_q));  // open: Qn, preset, en
  and and_1 (and_1_out, not_1_out, B, not_2_out);
  or or_1 (or_1_out, and_2_out, and_3_out);
  or or_2 (or_2_out, and_4_out, and_5_out, and_6_out, and_7_out);
  T_Flip_Flop t_ff_2 (.clk(clock_1_out), .T(and_1_out), .Q(A), .reset(t_ff_1_q));  // open: Qn, preset, en
  not not_1 (not_1_out, A);
  not not_2 (not_2_out, C);
  T_Flip_Flop t_ff_3 (.clk(clock_1_out), .T(or_1_out), .Q(B), .reset(t_ff_1_q));  // open: Qn, preset, en
  not not_3 (not_3_out, A);
  and and_2 (and_2_out, not_3_out, C, not_4_out);
  not not_4 (not_4_out, B);
  and and_3 (and_3_out, A, B, C);
  T_Flip_Flop t_ff_4 (.clk(clock_1_out), .T(or_2_out), .Q(C), .reset(t_ff_1_q));  // open: Qn, preset, en
  and and_4 (and_4_out, not_5_out, not_6_out, not_7_out);
  and and_5 (and_5_out, not_8_out, B, C);
  and and_6 (and_6_out, A, B, not_9_out);
  not not_5 (not_5_out, A);
  not not_6 (not_6_out, B);
  not not_7 (not_7_out, C);
  not not_8 (not_8_out, A);
  not not_9 (not_9_out, C);
  not not_10 (not_10_out, B);
  and and_7 (and_7_out, A, not_10_out, C);
  and and_8 (and_8_out, A, not_11_out, not_12_out);
  not not_11 (not_11_out, B);
  not not_12 (not_12_out, C);
endmodule

module D (
  input  Ck,
  output A,
  output B,
  output C
);

  wire and_1_out, and_2_out, and_3_out, and_4_out, and_5_out, and_6_out, and_7_out, d_ff_1_q, not_1_out,
       not_2_out, not_3_out, not_4_out, not_5_out, not_6_out, not_7_out, or_1_out, or_2_out, or_3_out;

  D_Flip_Flop d_ff_1 (.clk(Ck), .D(and_1_out), .Q(d_ff_1_q), .reset(d_ff_1_q));  // open: Qn, preset, en
  and and_1 (and_1_out, A, not_1_out, not_2_out);
  not not_1 (not_1_out, B);
  not not_2 (not_2_out, C);
  or or_1 (or_1_out, and_2_out, and_3_out);
  or or_2 (or_2_out, and_4_out, and_5_out);
  or or_3 (or_3_out, and_6_out, and_7_out);
  and and_2 (and_2_out, not_6_out, not_7_out);
  and and_3 (and_3_out, A, B);
  D_Flip_Flop d_ff_2 (.clk(Ck), .D(or_2_out), .Q(A), .reset(d_ff_1_q));  // open: Qn, preset, en
  and and_4 (and_4_out, B, not_3_out);
  not not_3 (not_3_out, C);
  and and_5 (and_5_out, C, A);
  D_Flip_Flop d_ff_3 (.clk(Ck), .D(or_3_out), .Q(B), .reset(d_ff_1_q));  // open: Qn, preset, en
  not not_4 (not_4_out, A);
  and and_6 (and_6_out, not_4_out, C);
  and and_7 (and_7_out, B, not_5_out);
  not not_5 (not_5_out, C);
  D_Flip_Flop d_ff_4 (.clk(Ck), .D(or_1_out), .Q(C), .reset(d_ff_1_q));  // open: Qn, preset, en
  not not_6 (not_6_out, A);
  not not_7 (not_7_out, B);
endmodule
