// Logisim project L11P50.circ as structural Verilog: 3 circuits, main circuit Decoder
module main (
  input  in_1,
  output out_2,
  output out_3,
  output out_4,
  output out_5,
  output out_6,
  output out_7,
  output out_8,
  output out_9
);

  wire clock_1_out, counter_1_a, counter_1_b, counter_1_c, counter_1_d, counter_2_full, decoder_1_alto,
       decoder_1_basso, decoder_1_centrale, decoder_1_dx_alto, decoder_1_dx_basso, decoder_1_sx_alt,
       decoder_1_sx_basso;

  Clock clock_1 (.out(clock_1_out));
  Counter counter_1 (
    .Ck(clock_1_out), .A(counter_1_a), .B(counter_1_b), .C(counter_1_c), .D(counter_1_d));  // open: En, Full
  Decoder decoder_1 (
    .A(counter_1_a), .B(counter_1_b), .C(counter_1_c), .D(counter_1_d), .Alto(decoder_1_alto),
    .DX_Basso(decoder_1_dx_basso), .Basso(decoder_1_basso), .SX_alt(decoder_1_sx_alt),
    .Centrale(decoder_1_centrale), .SX_basso(decoder_1_sx_basso), .DX_alto(decoder_1_dx_alto));
  _7_Segment_Display u_7_segment_display_1 (
    .g(decoder_1_centrale), .f(decoder_1_sx_alt), .a(decoder_1_alto), .b(decoder_1_dx_alto),
    .e(decoder_1_sx_basso), .d(decoder_1_basso), .c(decoder_1_dx_basso));  // open: dp
  Counter counter_2 (.Ck(clock_1_out), .En(in_1), .A(out_5), .B(out_4), .C(out_3), .D(out_2), .Full(counter_2_full));
  Counter counter_3 (.Ck(clock_1_out), .En(counter_2_full), .A(out_9), .B(out_8), .C(out_7), .D(out_6));  // open: Full
endmodule

module Decoder (
  input  A,
  input  B,
  input  C,
  input  D,
  output Alto,
  output Basso,
  output Centrale,
  output DX_alto,
  output DX_Basso,
  output SX_alt,
  output SX_basso
);

  wire A_C, B_C, B_CD, C_D, CD, minus_A, minus_A_B, minus_A_BC, minus_AB, minus_B, minus_B_D, minus_C,
       minus_C_D, minus_D;

  not not_1 (minus_A, A);
  not not_2 (minus_B, B);
  not not_3 (minus_C, C);
  not not_4 (minus_D, D);
  or or_1 (Alto, A_C, C, minus_B_D, B_CD);
  or or_2 (DX_Basso, minus_C, D, minus_AB);
  and u_A_C (A_C, A, minus_C);
  and u_CD (CD, C, D);
  and u_minus_C_D (minus_C_D, minus_C, minus_D);
  or or_3 (Basso, C_D, minus_B_D, A, B_CD, minus_A_BC);
  or or_4 (SX_alt, A_C, minus_AB, minus_C_D);
  and u_B_CD (B_CD, B, minus_C, D);
  and u_B_C (B_C, B, minus_C);
  and u_minus_A_BC (minus_A_BC, minus_A, minus_B, C);
  or or_5 (Centrale, A_C, C_D, minus_A_BC, B_C);
  or or_6 (SX_basso, C_D, minus_B_D);
  and u_minus_A_B (minus_A_B, minus_A, minus_B);
  and u_minus_B_D (minus_B_D, minus_B, minus_D);
  and u_C_D (C_D, C, minus_D);
  and u_minus_AB (minus_AB, minus_A, B);
  or or_7 (DX_alto, minus_A_B, minus_C_D, CD, A_C);
endmodule

module Counter (
  input  Ck,
  input  En,
  output A,
  output B,
  output C,
  output D,
  output Full
);

  wire and_1_out, and_2_out, and_3_out, and_4_out, and_5_out, not_1_out;

  and and_1 (and_1_out, Ck, En);
  T_Flip_Flop t_ff_1 (.clk(and_1_out), .T(and_5_out), .Q(Full), .reset(Full));  // open: Qn, preset, en
  T_Flip_Flop t_ff_2 (.clk(and_1_out), .T(and_2_out), .Q(A), .reset(Full));  // open: Qn, preset, en
  and and_2 (and_2_out, D, C, B);
  T_Flip_Flop t_ff_3 (.clk(and_1_out), .T(and_3_out), .Q(B), .reset(Full));  // open: Qn, preset, en
  and and_3 (and_3_out, D, C);
  T_Flip_Flop t_ff_4 (.clk(and_1_out), .T(and_4_out), .Q(C), .reset(Full));  // open: Qn, preset, en
  not not_1 (not_1_out, A);
  and and_4 (and_4_out, not_1_out, D);
  T_Flip_Flop t_ff_5 (.clk(and_1_out), .T(1'b1), .Q(D), .reset(Full));  // open: Qn, preset, en
  and and_5 (and_5_out, D, A);
endmodule
