// Logisim project L11P51.circ as structural Verilog: 8 circuits, main circuit main
module main (
  input  En,
  input  UP_DOWN,
  output A0,
  output A1,
  output A2,
  output A3
);

  wire clock_1_out, counter_1_full, counter_2_a0, counter_2_a1, counter_2_a2, counter_2_a3, decoder_1_alto,
       decoder_1_basso, decoder_1_centrale, decoder_1_dx_alto, decoder_1_dx_basso, decoder_1_sx_alt,
       decoder_1_sx_basso, decoder_2_alto, decoder_2_basso, decoder_2_centrale, decoder_2_dx_alto,
       decoder_2_dx_basso, decoder_2_sx_alt, decoder_2_sx_basso;

  Clock clock_1 (.out(clock_1_out));
  Counter counter_1 (
    .Ck(clock_1_out), .En(En), .UP_DOWN(UP_DOWN), .A0(A0), .A1(A1), .A2(A2), .A3(A3), .Full(counter_1_full));
  Counter counter_2 (
    .Ck(clock_1_out), .En(counter_1_full), .UP_DOWN(UP_DOWN), .A0(counter_2_a0), .A1(counter_2_a1),
    .A2(counter_2_a2), .A3(counter_2_a3));  // open: Full
  Decoder decoder_1 (
    .A(counter_2_a3), .B(counter_2_a2), .C(counter_2_a1), .D(counter_2_a0), .Alto(decoder_1_alto),
    .DX_Basso(decoder_1_dx_basso), .Basso(decoder_1_basso), .SX_alt(decoder_1_sx_alt),
    .Centrale(decoder_1_centrale), .SX_basso(decoder_1_sx_basso), .DX_alto(decoder_1_dx_alto));
  _7_Segment_Display u_7_segment_display_1 (
    .g(decoder_1_centrale), .f(decoder_1_sx_alt), .a(decoder_1_alto), .b(decoder_1_dx_alto),
    .e(decoder_1_sx_basso), .d(decoder_1_basso), .c(decoder_1_dx_basso));  // open: dp
  Decoder decoder_2 (
    .A(A3), .B(A2), .C(A1), .D(A0), .Alto(decoder_2_alto), .DX_Basso(decoder_2_dx_basso),
    .Basso(decoder_2_basso), .SX_alt(decoder_2_sx_alt), .Centrale(decoder_2_centrale),
    .SX_basso(decoder_2_sx_basso), .DX_alto(decoder_2_dx_alto));
  _7_Segment_Display u_7_segment_display_2 (
    .g(decoder_2_centrale), .f(decoder_2_sx_alt), .a(decoder_2_alto), .b(decoder_2_dx_alto),
    .e(decoder_2_sx_basso), .d(decoder_2_basso), .c(decoder_2_dx_basso));  // open: dp
endmodule

module A0 (
  input  Ck,
  input  En,
  input  Cl,
  input  UP_DOWN,
  output A0
);

  wire and_1_out, bitselector_1_out, not_1_out;

  and and_1 (and_1_out, Ck, En);
  BitSelector #(.width(1)) bitselector_1 (.in(Cl), .out(bitselector_1_out), .sel(not_1_out));
  not not_1 (not_1_out, UP_DOWN);
  T_Flip_Flop t_ff_1 (.clk(and_1_out), .T(1'b1), .Q(A0), .reset(bitselector_1_out));  // open: Qn, preset, en
endmodule

module A1 (
  input  Ck,
  input  En,
  input  UP_DOWN,
  input  A0,
  input  Cl,
  output A1
);

  wire and_1_out, multiplexer_1_out, not_1_out;

  and and_1 (and_1_out, Ck, En);
  Multiplexer multiplexer_1 (.in0(not_1_out), .in1(A0), .out(multiplexer_1_out), .sel(UP_DOWN), .en(En));
  not not_1 (not_1_out, A0);
  T_Flip_Flop t_ff_1 (.clk(and_1_out), .T(multiplexer_1_out), .Q(A1), .reset(Cl));  // open: Qn, preset, en
endmodule

module A2 (
  input  Ck,
  input  En,
  input  UP_DOWN,
  input  A1,
  input  A0,
  input  Cl,
  output A2
);

  wire and_1_out, and_2_out, and_3_out, multiplexer_1_out, not_1_out, not_2_out;

  and and_1 (and_1_out, Ck, En);
  not not_1 (not_1_out, A0);
  not not_2 (not_2_out, A1);
  and and_2 (and_2_out, not_1_out, not_2_out);
  and and_3 (and_3_out, A1, A0);
  Multiplexer multiplexer_1 (.in0(and_2_out), .in1(and_3_out), .out(multiplexer_1_out), .sel(UP_DOWN), .en(En));
  T_Flip_Flop t_ff_1 (.clk(and_1_out), .T(multiplexer_1_out), .Q(A2), .reset(Cl));  // open: Qn, preset, en
endmodule

module Counter (
  input  Ck,
  input  En,
  input  UP_DOWN,
  output A0,
  output A1,
  output A2,
  output A3,
  output Full
);

  A0 a0_1 (.Ck(Ck), .En(En), .Cl(Full), .A0(A0), .UP_DOWN(UP_DOWN));
  A1 a1_1 (.Ck(Ck), .En(En), .UP_DOWN(UP_DOWN), .A0(A0), .Cl(Full), .A1(A1));
  A2 a2_1 (.Ck(Ck), .En(En), .UP_DOWN(UP_DOWN), .A1(A1), .A0(A0), .Cl(Full), .A2(A2));
  A3 a3_1 (.Ck(Ck), .En(En), .UP_DOWN(UP_DOWN), .A0(A0), .A1(A1), .A2(A2), .Cl(Full), .A3(A3));
  Full full_1 (.A0(A0), .A1(A1), .A2(A2), .A3(A3), .UP_DOWN(UP_DOWN), .En(En), .Full(Full));
endmodule

module A3 (
  input  Ck,
  input  En,
  input  UP_DOWN,
  input  A0,
  input  A1,
  input  A2,
  input  Cl,
  output A3
);

  wire and_1_out, and_2_out, and_3_out, and_4_out, bitselector_1_out, multiplexer_1_out, not_1_out,
       not_2_out, not_3_out, not_4_out, not_5_out, or_1_out;

  not not_1 (not_1_out, UP_DOWN);
  and and_1 (and_1_out, Ck, En);
  and and_2 (and_2_out, not_1_out, Cl);
  BitSelector #(.width(1)) bitselector_1 (.in(Cl), .out(bitselector_1_out), .sel(not_2_out));
  not not_2 (not_2_out, UP_DOWN);
  or or_1 (or_1_out, and_2_out, multiplexer_1_out);
  Multiplexer multiplexer_1 (.in0(and_3_out), .in1(and_4_out), .out(multiplexer_1_out), .sel(UP_DOWN), .en(En));
  and and_3 (and_3_out, not_3_out, not_4_out, not_5_out);
  not not_3 (not_3_out, A2);
  not not_4 (not_4_out, A1);
  not not_5 (not_5_out, A0);
  and and_4 (and_4_out, A0, A1, A2);
  T_Flip_Flop t_ff_1 (.clk(and_1_out), .T(or_1_out), .Q(A3), .reset(bitselector_1_out));  // open: Qn, preset, en
endmodule

module Decoder (
  input  A,
  input  B,
  input  C,
  input  D,
  output Alto,
  output Basso,
  output Centrale,
  output DX_alto,
  output DX_Basso,
  output SX_alt,
  output SX_basso
);

  wire A_C, B_C, B_CD, C_D, CD, minus_A, minus_A_B, minus_A_BC, minus_AB, minus_B, minus_B_D, minus_C,
       minus_C_D, minus_D;

  not not_1 (minus_A, A);
  not not_2 (minus_B, B);
  not not_3 (minus_C, C);
  not not_4 (minus_D, D);
  or or_1 (Alto, A_C, C, minus_B_D, B_CD);
  or or_2 (DX_Basso, minus_C, D, minus_AB);
  and u_A_C (A_C, A, minus_C);
  and u_CD (CD, C, D);
  and u_minus_C_D (minus_C_D, minus_C, minus_D);
  or or_3 (Basso, C_D, minus_B_D, A, B_CD, minus_A_BC);
  or or_4 (SX_alt, A_C, minus_AB, minus_C_D);
  and u_B_CD (B_CD, B, minus_C, D);
  and u_B_C (B_C, B, minus_C);
  and u_minus_A_BC (minus_A_BC, minus_A, minus_B, C);
  or or_5 (Centrale, A_C, C_D, minus_A_BC, B_C);
  or or_6 (SX_basso, C_D, minus_B_D);
  and u_minus_A_B (minus_A_B, minus_A, minus_B);
  and u_minus_B_D (minus_B_D, minus_B, minus_D);
  and u_C_D (C_D, C, minus_D);
  and u_minus_AB (minus_AB, minus_A, B);
  or or_7 (DX_alto, minus_A_B, minus_C_D, CD, A_C);
endmodule

module Full (
  input  A0,
  input  A1,
  input  A2,
  input  A3,
  input  UP_DOWN,
  input  En,
  output Full
);

  wire and_1_out, and_2_out, not_1_out, not_2_out, not_3_out, not_4_out, not_5_out, not_6_out;

  not not_1 (not_1_out, A0);
  not not_2 (not_2_out, A1);
  and and_1 (and_1_out, not_1_out, not_2_out, not_3_out, not_4_out);
  not not_3 (not_3_out, A2);
  not not_4 (not_4_out, A3);
  not not_5 (not_5_out, A2);
  and and_2 (and_2_out, A3, not_5_out, A1, not_6_out);
  not not_6 (not_6_out, A0);
  Multiplexer multiplexer_1 (.in0(and_1_out), .in1(and_2_out), .out(Full), .sel(UP_DOWN), .en(En));
endmodule
