// Logisim project L13P63.circ as structural Verilog: 1 circuit, main circuit main
module main (
  input  En
);

  wire and_1_out, and_2_out, and_3_out, clock_1_out, d_ff_1_q, d_ff_2_q, d_ff_3_q, d_ff_4_q, d_ff_5_q,
       d_ff_5_qn, d_ff_6_q, not_1_out;

  Clock clock_1 (.out(clock_1_out));
  and and_1 (and_1_out, clock_1_out, and_2_out);
  and and_2 (and_2_out, En, not_1_out);
  not not_1 (not_1_out, d_ff_6_q);
  and and_3 (and_3_out, En, d_ff_6_q);
  LED led_1 (.in(d_ff_1_q));
  D_Flip_Flop d_ff_1 (.clk(and_1_out), .D(d_ff_5_qn), .Q(d_ff_1_q), .reset(and_3_out));  // open: Qn, preset, en
  LED led_2 (.in(d_ff_2_q));
  D_Flip_Flop d_ff_2 (.clk(and_1_out), .D(d_ff_1_q), .Q(d_ff_2_q), .reset(and_3_out));  // open: Qn, preset, en
  D_Flip_Flop d_ff_3 (.clk(and_1_out), .D(d_ff_2_q), .Q(d_ff_3_q), .reset(and_3_out));  // open: Qn, preset, en
  LED led_3 (.in(d_ff_3_q));
  LED led_4 (.in(d_ff_4_q));
  D_Flip_Flop d_ff_4 (.clk(and_1_out), .D(d_ff_3_q), .Q(d_ff_4_q), .reset(and_3_out));  // open: Qn, preset, en
  D_Flip_Flop d_ff_5 (
    .clk(and_1_out), .D(d_ff_4_q), .Q(d_ff_5_q), .Qn(d_ff_5_qn), .reset(and_3_out));  // open: preset, en
  D_Flip_Flop d_ff_6 (.clk(and_1_out), .D(d_ff_5_q), .Q(d_ff_6_q));  // open: Qn, preset, en, reset
  LED led_5 (.in(d_ff_5_q));
endmodule
