// Logisim project L13P65.circ as structural Verilog: 1 circuit, main circuit main
module main (
);

  wire and_1_out, clock_1_out, d_ff_1_q, d_ff_2_q, not_1_out, or_1_out, or_2_out, shift_register_1_out;

  Clock clock_1 (.out(clock_1_out));
  Shift_Register shift_register_1 (
    .clk(clock_1_out), .out(shift_register_1_out));  // open: shift, in, load, clr, d0, q0, d1, q1, d2, q2, d3, q3, d4, q4, d5, q5, d6, q6, d7, q7
  D_Flip_Flop d_ff_1 (.clk(clock_1_out), .D(or_1_out), .Q(d_ff_1_q));  // open: Qn, preset, en, reset
  not not_1 (not_1_out, shift_register_1_out);
  or or_1 (or_1_out, not_1_out, d_ff_2_q);
  or or_2 (or_2_out, shift_register_1_out, d_ff_1_q);
  and and_1 (and_1_out, d_ff_1_q, d_ff_2_q);
  D_Flip_Flop d_ff_2 (.clk(clock_1_out), .D(or_2_out), .Q(d_ff_2_q));  // open: Qn, preset, en, reset
  LED led_1 (.in(and_1_out));
endmodule
