// Logisim project L13P66.circ as structural Verilog: 1 circuit, main circuit main
module main (
  input  En,
  output Z2,
  output Z1
);

  wire and_1_out, and_2_out, and_3_out, and_4_out, and_5_out, and_6_out, and_7_out, and_8_out, and_9_out,
       and_10_out, and_11_out, and_12_out, and_13_out, and_14_out, and_15_out, and_16_out, clock_1_out,
       d_ff_1_qn, d_ff_2_q, d_ff_2_qn, d_ff_3_qn, d_ff_4_q, d_ff_4_qn, not_1_out, not_2_out, not_3_out,
       or_1_out, or_2_out, or_3_out, shift_register_1_out, t_ff_1_q;

  Clock clock_1 (.out(clock_1_out));
  and and_1 (and_1_out, clock_1_out, En);
  Shift_Register shift_register_1 (
    .clk(and_1_out), .out(shift_register_1_out));  // open: shift, in, load, clr, d0, q0, d1, q1, d2, q2, d3, q3, d4, q4, d5, q5, d6, q6, d7, q7
  and and_2 (and_2_out, and_6_out, not_1_out);
  and and_3 (and_3_out, and_7_out, not_1_out);
  not not_1 (not_1_out, shift_register_1_out);
  and and_4 (and_4_out, shift_register_1_out, d_ff_2_q);
  and and_5 (and_5_out, and_1_out, d_ff_1_qn);
  and and_6 (and_6_out, d_ff_2_q, d_ff_2_q, t_ff_1_q);
  and and_7 (and_7_out, d_ff_4_q, d_ff_2_q, not_2_out);
  not not_2 (not_2_out, t_ff_1_q);
  T_Flip_Flop t_ff_1 (.clk(and_1_out), .T(or_1_out), .Q(t_ff_1_q));  // open: Qn, preset, reset, en
  or or_1 (or_1_out, and_4_out, and_8_out);
  and and_8 (and_8_out, d_ff_4_qn, t_ff_1_q);
  D_Flip_Flop d_ff_1 (.clk(and_5_out), .D(and_3_out), .Q(Z2), .Qn(d_ff_1_qn));  // open: preset, en, reset
  and and_9 (and_9_out, shift_register_1_out, d_ff_4_q);
  or or_2 (or_2_out, and_9_out, and_10_out, and_12_out);
  and and_10 (and_10_out, d_ff_2_q, not_3_out);
  not not_3 (not_3_out, shift_register_1_out);
  and and_11 (and_11_out, d_ff_1_qn, and_2_out);
  D_Flip_Flop d_ff_2 (.clk(and_1_out), .D(or_2_out), .Q(d_ff_2_q), .Qn(d_ff_2_qn));  // open: preset, en, reset
  and and_12 (and_12_out, shift_register_1_out, d_ff_4_q, d_ff_2_qn);
  and and_13 (and_13_out, t_ff_1_q, d_ff_2_qn);
  and and_14 (and_14_out, and_1_out, d_ff_3_qn);
  or or_3 (or_3_out, and_13_out, and_16_out, and_15_out);
  and and_15 (and_15_out, d_ff_4_qn, d_ff_2_qn, shift_register_1_out);
  and and_16 (and_16_out, d_ff_2_qn, d_ff_4_q);
  D_Flip_Flop d_ff_3 (.clk(and_14_out), .D(and_11_out), .Q(Z1), .Qn(d_ff_3_qn));  // open: preset, en, reset
  D_Flip_Flop d_ff_4 (.clk(and_1_out), .D(or_3_out), .Q(d_ff_4_q), .Qn(d_ff_4_qn));  // open: preset, en, reset
endmodule
