// Logisim project L13P67.circ as structural Verilog: 3 circuits, main circuit main
module main (
  input  En
);

  wire and_1_out, and_2_out, and_3_out, and_4_out, Ck_out, not_1_out, not_2_out, not_3_out, not_4_out,
       not_5_out, not_6_out, or_1_out, shift_register_1_out, shift_register_2_out, t_ff_1_q, t_ff_1_qn,
       x1_1__01, x1_1__10, x1_1__11, x2_1__00;

  Clock Ck (.out(Ck_out));
  and and_1 (and_1_out, En, Ck_out);
  and and_2 (and_2_out, not_1_out, x1_1__11, not_2_out, t_ff_1_qn);
  not not_1 (not_1_out, x1_1__01);
  Shift_Register shift_register_1 (
    .clk(and_1_out), .out(shift_register_1_out));  // open: shift, in, load, clr, d0, q0, d1, q1, d2, q2, d3, q3, d4, q4, d5, q5, d6, q6, d7, q7
  Shift_Register shift_register_2 (
    .clk(and_1_out), .out(shift_register_2_out));  // open: shift, in, load, clr, d0, q0, d1, q1, d2, q2, d3, q3, d4, q4, d5, q5, d6, q6, d7, q7
  not not_2 (not_2_out, x1_1__10);
  not not_3 (not_3_out, x1_1__11);
  and and_3 (and_3_out, not_5_out, not_4_out, x1_1__10);
  not not_4 (not_4_out, x1_1__11);
  not not_5 (not_5_out, x1_1__01);
  and and_4 (and_4_out, x1_1__01, not_3_out, not_6_out, t_ff_1_q);
  not not_6 (not_6_out, x1_1__10);
  X2 x2_1 (.En(En), .CK(and_1_out), .R(shift_register_1_out), ._00(x2_1__00));
  X1 x1_1 (.En(x2_1__00), .Ck(and_1_out), .R(shift_register_2_out), ._01(x1_1__01), ._10(x1_1__10), ._11(x1_1__11));
  or or_1 (or_1_out, and_2_out, and_4_out, and_3_out);
  T_Flip_Flop t_ff_1 (.clk(and_1_out), .T(or_1_out), .Q(t_ff_1_q), .Qn(t_ff_1_qn));  // open: preset, reset, en
  LED led_1 (.in(t_ff_1_q));

  // Notes on the sheet:
  //   Z
endmodule

module X2 (
  input  En,
  input  CK,
  input  R,
  output _00
);

  wire and_1_out, and_2_out, and_3_out, d_ff_1_q, d_ff_1_qn, d_ff_2_q, d_ff_2_qn, not_1_out, or_1_out;

  and and_1 (and_1_out, En, CK);
  not not_1 (not_1_out, R);
  and and_2 (and_2_out, not_1_out, or_1_out);
  or or_1 (or_1_out, d_ff_1_q, d_ff_2_q);
  D_Flip_Flop d_ff_1 (.clk(and_1_out), .D(and_2_out), .Q(d_ff_1_q), .Qn(d_ff_1_qn));  // open: preset, en, reset
  and and_3 (and_3_out, d_ff_1_qn, not_1_out, d_ff_2_qn);
  D_Flip_Flop d_ff_2 (.clk(and_1_out), .D(and_3_out), .Q(d_ff_2_q), .Qn(d_ff_2_qn));  // open: preset, en, reset
  and and_4 (_00, d_ff_2_qn, d_ff_1_q);

  // Notes on the sheet:
  //   A
  //   B
endmodule

module X1 (
  input  En,
  input  Ck,
  input  R,
  output _01,
  output _10,
  output _11
);

  wire and_1_out, and_2_out, and_4_out, and_6_out, d_ff_1_q, d_ff_1_qn, d_ff_2_q, d_ff_2_qn, d_ff_3_q,
       d_ff_3_qn, not_1_out, or_1_out, or_2_out, or_3_out;

  and and_1 (and_1_out, En, Ck);
  or or_1 (or_1_out, d_ff_2_q, and_2_out);
  and and_2 (and_2_out, d_ff_1_q, d_ff_3_qn);
  and and_3 (_01, d_ff_1_qn, d_ff_2_q, d_ff_3_q);
  D_Flip_Flop d_ff_1 (.clk(and_1_out), .D(or_1_out), .Q(d_ff_1_q), .Qn(d_ff_1_qn));  // open: preset, en, reset
  or or_2 (or_2_out, d_ff_3_q, d_ff_1_qn);
  and and_4 (and_4_out, or_2_out, d_ff_2_qn, R);
  and and_5 (_10, d_ff_1_q, d_ff_2_qn, d_ff_3_q);
  D_Flip_Flop d_ff_2 (.clk(and_1_out), .D(and_4_out), .Q(d_ff_2_q), .Qn(d_ff_2_qn));  // open: preset, en, reset
  and and_6 (and_6_out, d_ff_3_q, R, d_ff_2_qn);
  and and_7 (_11, d_ff_1_q, d_ff_3_qn, d_ff_2_qn);
  or or_3 (or_3_out, and_6_out, not_1_out);
  not not_1 (not_1_out, R);
  D_Flip_Flop d_ff_3 (.clk(and_1_out), .D(or_3_out), .Q(d_ff_3_q), .Qn(d_ff_3_qn));  // open: preset, en, reset

  // Notes on the sheet:
  //   A
  //   B
  //   C
endmodule
