// Logisim project L7P16.circ as structural Verilog: 1 circuit, main circuit main
module main (
  input  [2:0] in_1,
  input  in_2,
  output out_3
);

  wire not_1_out;

  not not_1 (not_1_out, 1'b1);
  Multiplexer #(.select(3)) multiplexer_1 (
    .in0(not_1_out), .in1(not_1_out), .in2(1'b1), .in3(1'b1), .in4(not_1_out), .in5(1'b1), .in6(1'b1),
    .in7(1'b1), .out(out_3), .sel(in_1), .en(in_2));
endmodule
