// Logisim project L7P20.circ as structural Verilog: 1 circuit, main circuit main
module main (
  input  C,
  input  B,
  input  A,
  input  in_4,
  output out_5
);

  wire not_1_out, not_2_out;

  not not_1 (not_1_out, C);
  Multiplexer #(.select(2)) multiplexer_1 (
    .in0(C), .in1(not_1_out), .in2(not_2_out), .in3(1'b1), .out(out_5), .sel({A, B}), .en(in_4));
  not not_2 (not_2_out, 1'b1);
endmodule
