// Logisim project L7P38.circ as structural Verilog: 1 circuit, main circuit main
module main (
  input  [4:0] in_1,
  output _0,
  output _0_2,
  output _0_3,
  output _1,
  output _0_4,
  output _2,
  output _0_5,
  output _3,
  output _0_6,
  output _4,
  output _0_7,
  output _5,
  output _0_8,
  output _6,
  output _0_9,
  output _7,
  output _0_10,
  output _0_11,
  output _0_12,
  output _0_13,
  output _0_14,
  output _0_15,
  output _0_16,
  output _0_17,
  output _0_18,
  output _0_19,
  output _0_20,
  output _0_21,
  output _0_22,
  output _0_23,
  output _0_24,
  output _0_25
);

  wire not_1_out;

  Decoder #(.select(4)) decoder_1 (
    .out0(_0), .out1(_0_3), .out2(_0_4), .out3(_0_5), .out4(_0_6), .out5(_0_7), .out6(_0_8), .out7(_0_9),
    .out8(_0_10), .out9(_0_12), .out10(_0_14), .out11(_0_16), .out12(_0_18), .out13(_0_20), .out14(_0_22),
    .out15(_0_24), .sel(in_1[3:0]), .en(in_1[4]));
  Decoder #(.select(4)) decoder_2 (
    .out0(_0_2), .out1(_1), .out2(_2), .out3(_3), .out4(_4), .out5(_5), .out6(_6), .out7(_7), .out8(_0_11),
    .out9(_0_13), .out10(_0_15), .out11(_0_17), .out12(_0_19), .out13(_0_21), .out14(_0_23), .out15(_0_25),
    .sel(in_1[3:0]), .en(not_1_out));
  not not_1 (not_1_out, in_1[4]);
endmodule
