// Logisim project L7P50.circ as structural Verilog: 1 circuit, main circuit main
module main (
  input  in_1,
  input  [1:0] in_2,
  output out_3
);

  wire decoder_1_out0, decoder_1_out1, decoder_2_out0, decoder_2_out2, decoder_2_out3, not_1_out;

  not not_1 (not_1_out, in_1);
  Decoder #(.select(2)) decoder_1 (
    .out0(decoder_1_out0), .out1(decoder_1_out1), .sel(in_2), .en(not_1_out));  // open: out2, out3
  Decoder #(.select(2)) decoder_2 (
    .out0(decoder_2_out0), .out2(decoder_2_out2), .out3(decoder_2_out3), .sel(in_2), .en(in_1));  // open: out1
  or or_1 (out_3, decoder_1_out0, decoder_1_out1, decoder_2_out0, decoder_2_out2, decoder_2_out3);
endmodule
