// Logisim project L7P54.circ as structural Verilog: 1 circuit, main circuit main
module main (
  input  _0,
  input  _1,
  input  _2,
  input  _3,
  output Y,
  output Z,
  output D
);

  or or_1 (Y, _2, _3);
  or or_2 (Z, _1, _3);
  or or_3 (D, _0, _1, _2, _3);
endmodule
