// Logisim project L7P8.circ as structural Verilog: 1 circuit, main circuit main
module main (
  input  in_1,
  input  in_2,
  input  in_3,
  input  in_4,
  input  in_5,
  input  in_6,
  input  in_7,
  input  in_8,
  input  in_9,
  input  in_10,
  input  in_11,
  input  in_12,
  input  in_13,
  input  in_14,
  input  in_15,
  input  in_16,
  input  D,
  input  C,
  input  B,
  input  A,
  output out_21,
  output out_22
);

  wire not_1_out;

  Multiplexer #(.select(3)) multiplexer_1 (
    .in0(in_1), .in1(in_3), .in2(in_5), .in3(in_7), .in4(in_9), .in5(in_11), .in6(in_13), .in7(in_15),
    .out(out_21), .sel({B, C, D}), .en(A));
  Multiplexer #(.select(3)) multiplexer_2 (
    .in0(in_2), .in1(in_4), .in2(in_6), .in3(in_8), .in4(in_10), .in5(in_12), .in6(in_14), .in7(in_16),
    .out(out_21), .sel({B, C, D}), .en(not_1_out));
  not not_1 (not_1_out, A);

  assign out_22 = out_21;
endmodule
