// Logisim project Parity.circ as structural Verilog: 2 circuits, main circuit main
module main (
  input  [6:0] in_1,
  output [7:0] out_2,
  output Even,
  output Odd
);

  Parity parity_1 (.in_1(in_1), .Odd(Odd), .Even(Even), .out_2(out_2));
endmodule

module Parity (
  input  [6:0] in_1,
  output [7:0] out_2,
  output Odd,
  output Even
);

  wire xor_1_out, xor_2_out, xor_3_out, xor_4_out, xor_5_out;

  xor xor_1 (xor_1_out, in_1[0], in_1[1]);
  xor xor_2 (xor_2_out, xor_1_out, in_1[2]);
  xor xor_3 (xor_3_out, xor_2_out, in_1[3]);
  xor xor_4 (xor_4_out, xor_3_out, in_1[4]);
  xor xor_5 (xor_5_out, xor_4_out, in_1[5]);
  xor xor_6 (Odd, in_1[6], xor_5_out);
  not not_1 (Even, Odd);

  assign out_2 = {Odd, in_1};
endmodule
