// Logisim project Subtractor.circ as structural Verilog: 1 circuit, main circuit main
module main (
  input  A,
  input  [3:0] X,
  input  [3:0] Y,
  output [4:0] M_S
);

  wire not_1_out, not_2_out;
  wire [3:0] controlled_buffer_1_out, controlled_buffer_3_out;

  assign controlled_buffer_1_out = not_1_out ? Y : 4'bz;  // Controlled_Buffer controlled_buffer_1
  not not_1 (not_1_out, A);
  assign controlled_buffer_1_out = A ? X : 4'bz;  // Controlled_Buffer controlled_buffer_2
  assign controlled_buffer_3_out = not_2_out ? X : 4'bz;  // Controlled_Buffer controlled_buffer_3
  not not_2 (not_2_out, A);
  assign controlled_buffer_3_out = A ? Y : 4'bz;  // Controlled_Buffer controlled_buffer_4
  Subtractor #(.width(4)) subtractor_1 (
    .a(controlled_buffer_1_out), .b(controlled_buffer_3_out), .out(M_S[3:0]), .bout(M_S[4]));  // open: bin
endmodule
