// Logisim project Valore assoluto.circ as structural Verilog: 1 circuit, main circuit main
module main (
  input  [3:0] in_1,
  input  in_2,
  output [3:0] out_3
);

  wire adder_1_out, adder_2_cout, adder_2_out, adder_3_cout, adder_3_out, adder_4_cout, adder_4_out,
       not_1_out, not_2_out, not_3_out, not_4_out;

  not not_1 (not_1_out, in_1[3]);
  Adder #(.width(1)) adder_1 (.a(not_1_out), .b(adder_2_cout), .out(adder_1_out));  // open: cin, cout
  Multiplexer multiplexer_1 (.in0(in_1[3]), .in1(adder_1_out), .out(out_3[3]), .sel(in_1[3]));  // open: en
  Multiplexer multiplexer_2 (.in0(in_1[2]), .in1(adder_2_out), .out(out_3[2]), .sel(in_1[3]));  // open: en
  not not_2 (not_2_out, in_1[2]);
  Adder #(.width(1)) adder_2 (.a(not_2_out), .b(adder_3_cout), .out(adder_2_out), .cout(adder_2_cout));  // open: cin
  Multiplexer multiplexer_3 (.in0(in_1[1]), .in1(adder_3_out), .out(out_3[1]), .sel(in_1[3]));  // open: en
  not not_3 (not_3_out, in_1[1]);
  Adder #(.width(1)) adder_3 (.a(not_3_out), .b(adder_4_cout), .out(adder_3_out), .cout(adder_3_cout));  // open: cin
  not not_4 (not_4_out, in_1[0]);
  Multiplexer multiplexer_4 (.in0(in_1[0]), .in1(adder_4_out), .out(out_3[0]), .sel(in_1[3]));  // open: en
  Adder #(.width(1)) adder_4 (.a(not_4_out), .b(in_2), .out(adder_4_out), .cout(adder_4_cout));  // open: cin
endmodule
