// Logisim project Porta NAND.circ as structural Verilog: 1 circuit, main circuit main
module main (
  input  A,
  input  A_2,
  input  A_3,
  input  B,
  input  B_2,
  input  A_4,
  input  B_3,
  output out_8,
  output out_9,
  output out_10,
  output out_11,
  output out_12,
  output out_13,
  output out_14,
  output out_15
);

  wire nand_1_out, nand_3_out, nand_4_out, nand_7_out, nand_8_out, nand_9_out;

  nand nand_1 (nand_1_out, A_2, B);
  and and_1 (out_12, A_2, B);
  nand nand_2 (out_8, A, A);
  not not_1 (out_9, A);
  nand nand_3 (nand_3_out, A_4, A_4);
  nand nand_4 (nand_4_out, B_3, B_3);
  or or_1 (out_15, A_4, B_3);
  nand nand_5 (out_10, nand_1_out, nand_1_out);
  nand nand_6 (out_14, nand_3_out, nand_4_out);
  nand nand_7 (nand_7_out, A_3, A_3);
  nand nand_8 (nand_8_out, B_2, B_2);
  nor nor_1 (out_13, A_3, B_2);
  nand nand_9 (nand_9_out, nand_7_out, nand_8_out);
  nand nand_10 (out_11, nand_9_out, nand_9_out);

  // Notes on the sheet:
  //   NOT using NAND
  //   AND using NAND
  //   OR using NAND
  //   NOR using NAND
endmodule
