// Logisim project Porta NOR.circ as structural Verilog: 1 circuit, main circuit main
module main (
  input  A,
  input  A_2,
  input  A_3,
  input  B,
  input  B_2,
  input  A_4,
  input  B_3,
  output out_8,
  output out_9,
  output out_10,
  output out_11,
  output out_12,
  output out_13,
  output out_14,
  output out_15
);

  wire nor_1_out, nor_2_out, nor_3_out, nor_7_out, nor_8_out, nor_9_out;

  not not_1 (out_9, A);
  nor nor_1 (nor_1_out, A_2, A_2);
  or or_1 (out_12, A_2, A_2);
  nor nor_2 (nor_2_out, A_4, A_4);
  nor nor_3 (nor_3_out, B_3, B_3);
  and and_1 (out_15, A_4, B_3);
  nor nor_4 (out_8, A, A);
  nor nor_5 (out_10, nor_1_out, nor_1_out);
  nor nor_6 (out_14, nor_2_out, nor_3_out);
  nor nor_7 (nor_7_out, A_3, A_3);
  nor nor_8 (nor_8_out, B_2, B_2);
  nand nand_1 (out_13, A_3, B_2);
  nor nor_9 (nor_9_out, nor_7_out, nor_8_out);
  nor nor_10 (out_11, nor_9_out, nor_9_out);

  assign B = A_2;

  // Notes on the sheet:
  //   NOT using NOR
  //   OR using NOR
  //   AND using NOR
  //   NAND using NOR
endmodule
