// Logisim project Tastierino.circ as structural Verilog: 2 circuits, main circuit main
module main (
  output out_1,
  output out_2,
  output out_3,
  output out_4
);

  wire _0, _1, _2, _3, _4, _5, _6, _7, _8, _9;

  Button u__7 (.out(_7));
  Button u__4 (.out(_4));
  Button u__1 (.out(_1));
  Button u__8 (.out(_8));
  Button u__9 (.out(_9));
  Button u__6 (.out(_6));
  Button u__5 (.out(_5));
  Button u__3 (.out(_3));
  Button u__2 (.out(_2));
  Button u__0 (.out(_0));
  converter converter_1 (
    .n1(_1), .n2(_2), .n3(_3), .n4(_4), .n5(_5), .n6(_6), .n7(_7), .n8(_8), .n9(_9), .n0(_0), .a(out_4),
    .b(out_3), .c(out_2), .d(out_1));

  // Other names for the same wires on the sheet: a = out_4; b = out_3; c = out_2; d = out_1
endmodule

module converter (
  input  n1,
  input  n2,
  input  n3,
  input  n4,
  input  n5,
  input  n6,
  input  n7,
  input  n8,
  input  n9,
  input  n0,
  output a,
  output b,
  output c,
  output d
);

  wire nand_1_out, nand_2_out, nand_3_out, nand_4_out, nand_5_out, nand_6_out, nand_7_out, nand_8_out,
       nand_9_out, nand_10_out, nand_11_out, nand_12_out, nand_13_out, nand_14_out, nand_15_out, nand_16_out,
       nand_17_out, nand_18_out, nand_19_out, nand_20_out, nand_21_out, nand_22_out, nand_23_out,
       nand_24_out, nand_25_out, nand_26_out, nand_27_out, nand_28_out, nand_29_out, nand_30_out,
       nand_31_out, nand_32_out, nand_33_out, nand_34_out, nand_35_out, nand_36_out, nand_37_out,
       nand_38_out, nand_39_out, nand_40_out, nand_41_out, nand_42_out, nand_43_out, nand_44_out,
       nand_45_out, nand_46_out, nand_47_out, nand_48_out, nand_49_out, nand_50_out, nand_51_out,
       nand_52_out, nand_53_out, nand_54_out, nand_55_out, nand_56_out, nand_57_out, nand_58_out,
       nand_59_out, nand_60_out, nand_61_out, nand_62_out, nand_63_out, nand_64_out, nand_65_out,
       nand_66_out, nand_67_out, nand_68_out, nand_69_out, nand_70_out, nand_71_out, nand_72_out,
       nand_73_out, nand_74_out, nand_75_out, nand_76_out, nand_77_out, nand_78_out, nand_79_out,
       nand_80_out, nand_81_out, nand_82_out, nand_83_out, nand_84_out, nand_85_out, nand_86_out,
       nand_87_out, nand_88_out, nand_89_out, nand_90_out, nand_91_out, nand_92_out, nand_93_out,
       nand_94_out, nand_95_out, nand_96_out, nand_97_out, nand_98_out, nand_99_out, nand_100_out,
       nand_101_out, nand_102_out, nand_103_out, nand_104_out;

  nand nand_1 (nand_1_out, n1, n1);
  nand nand_2 (nand_2_out, n2, n2);
  nand nand_3 (nand_3_out, n3, n3);
  nand nand_4 (nand_4_out, n4, n4);
  nand nand_5 (nand_5_out, n5, n5);
  nand nand_6 (nand_6_out, n6, n6);
  nand nand_7 (nand_7_out, n7, n7);
  nand nand_8 (nand_8_out, n0, n0);
  nand nand_9 (nand_9_out, n1, n1);
  nand nand_10 (nand_10_out, n2, n2);
  nand nand_11 (nand_11_out, n3, n3);
  nand nand_12 (nand_12_out, n4, n4);
  nand nand_13 (nand_13_out, n5, n5);
  nand nand_14 (nand_14_out, n6, n6);
  nand nand_15 (nand_15_out, n7, n7);
  nand nand_16 (nand_16_out, n0, n0);
  nand nand_17 (nand_17_out, n1, n1);
  nand nand_18 (nand_18_out, n2, n2);
  nand nand_19 (nand_19_out, n3, n3);
  nand nand_20 (nand_20_out, n8, n8);
  nand nand_21 (nand_21_out, n9, n9);
  nand nand_22 (nand_22_out, n0, n0);
  nand nand_23 (nand_23_out, n1, n1);
  nand nand_24 (nand_24_out, n2, n2);
  nand nand_25 (nand_25_out, n3, n3);
  nand nand_26 (nand_26_out, n8, n8);
  nand nand_27 (nand_27_out, n9, n9);
  nand nand_28 (nand_28_out, n0, n0);
  nand nand_29 (nand_29_out, n1, n1);
  nand nand_30 (nand_30_out, n2, n2);
  nand nand_31 (nand_31_out, n3, n3);
  nand nand_32 (nand_32_out, n8, n8);
  nand nand_33 (nand_33_out, n9, n9);
  nand nand_34 (nand_34_out, n0, n0);
  nand nand_35 (nand_35_out, n1, n1);
  nand nand_36 (nand_36_out, n2, n2);
  nand nand_37 (nand_37_out, n3, n3);
  nand nand_38 (nand_38_out, n8, n8);
  nand nand_39 (nand_39_out, n9, n9);
  nand nand_40 (nand_40_out, n0, n0);
  nand nand_41 (nand_41_out, n1, n1);
  nand nand_42 (nand_42_out, n4, n4);
  nand nand_43 (nand_43_out, n5, n5);
  nand nand_44 (nand_44_out, n8, n8);
  nand nand_45 (nand_45_out, n9, n9);
  nand nand_46 (nand_46_out, n0, n0);
  nand nand_47 (nand_47_out, n1, n1);
  nand nand_48 (nand_48_out, n4, n4);
  nand nand_49 (nand_49_out, n5, n5);
  nand nand_50 (nand_50_out, n8, n8);
  nand nand_51 (nand_51_out, n9, n9);
  nand nand_52 (nand_52_out, n0, n0);
  nand nand_53 (nand_53_out, n1, n1);
  nand nand_54 (nand_54_out, n4, n4);
  nand nand_55 (nand_55_out, n5, n5);
  nand nand_56 (nand_56_out, n8, n8);
  nand nand_57 (nand_57_out, n9, n9);
  nand nand_58 (nand_58_out, n0, n0);
  nand nand_59 (nand_59_out, n1, n1);
  nand nand_60 (nand_60_out, n4, n4);
  nand nand_61 (nand_61_out, n5, n5);
  nand nand_62 (nand_62_out, n8, n8);
  nand nand_63 (nand_63_out, n9, n9);
  nand nand_64 (nand_64_out, n0, n0);
  nand nand_65 (nand_65_out, n2, n2);
  nand nand_66 (nand_66_out, n4, n4);
  nand nand_67 (nand_67_out, n6, n6);
  nand nand_68 (nand_68_out, n8, n8);
  nand nand_69 (nand_69_out, n0, n0);
  nand nand_70 (nand_70_out, n2, n2);
  nand nand_71 (nand_71_out, n4, n4);
  nand nand_72 (nand_72_out, n6, n6);
  nand nand_73 (nand_73_out, n8, n8);
  nand nand_74 (nand_74_out, n0, n0);
  nand nand_75 (nand_75_out, n2, n2);
  nand nand_76 (nand_76_out, n4, n4);
  nand nand_77 (nand_77_out, n6, n6);
  nand nand_78 (nand_78_out, n8, n8);
  nand nand_79 (nand_79_out, n0, n0);
  nand nand_80 (nand_80_out, n2, n2);
  nand nand_81 (nand_81_out, n4, n4);
  nand nand_82 (nand_82_out, n6, n6);
  nand nand_83 (nand_83_out, n8, n8);
  nand nand_84 (nand_84_out, n0, n0);
  nand nand_85 (nand_85_out, n2, n2);
  nand nand_86 (nand_86_out, n4, n4);
  nand nand_87 (nand_87_out, n6, n6);
  nand nand_88 (nand_88_out, n8, n8);
  nand nand_89 (nand_89_out, n0, n0);
  nand nand_90 (nand_90_out, nand_1_out, nand_2_out, nand_3_out, nand_4_out, nand_5_out, nand_6_out, nand_7_out, n9, nand_8_out);
  nand nand_91 (nand_91_out, nand_9_out, nand_10_out, nand_11_out, nand_12_out, nand_13_out, nand_14_out, nand_15_out, n8, nand_16_out);
  nand nand_92 (nand_92_out, nand_17_out, nand_18_out, nand_19_out, n7, nand_20_out, nand_21_out, nand_22_out);
  nand nand_93 (nand_93_out, nand_23_out, nand_24_out, nand_25_out, n6, nand_26_out, nand_27_out, nand_28_out);
  nand nand_94 (nand_94_out, nand_29_out, nand_30_out, nand_31_out, n5, nand_32_out, nand_33_out, nand_34_out);
  nand nand_95 (nand_95_out, nand_35_out, nand_36_out, nand_37_out, n4, nand_38_out, nand_39_out, nand_40_out);
  nand nand_96 (nand_96_out, nand_41_out, nand_42_out, nand_43_out, n7, nand_44_out, nand_45_out, nand_46_out);
  nand nand_97 (nand_97_out, nand_47_out, nand_48_out, nand_49_out, n6, nand_50_out, nand_51_out, nand_52_out);
  nand nand_98 (nand_98_out, nand_53_out, n3, nand_54_out, nand_55_out, nand_56_out, nand_57_out, nand_58_out);
  nand nand_99 (nand_99_out, nand_59_out, n2, nand_60_out, nand_61_out, nand_62_out, nand_63_out, nand_64_out);
  nand nand_100 (nand_100_out, nand_65_out, nand_66_out, nand_67_out, nand_68_out, n9, nand_69_out);
  nand nand_101 (nand_101_out, nand_70_out, nand_71_out, nand_72_out, n7, nand_73_out, nand_74_out);
  nand nand_102 (nand_102_out, nand_75_out, nand_76_out, n5, nand_77_out, nand_78_out, nand_79_out);
  nand nand_103 (nand_103_out, nand_80_out, n3, nand_81_out, nand_82_out, nand_83_out, nand_84_out);
  nand nand_104 (nand_104_out, n1, nand_85_out, nand_86_out, nand_87_out, nand_88_out, nand_89_out);
  nand nand_105 (a, nand_90_out, nand_91_out);
  nand nand_106 (b, nand_92_out, nand_93_out, nand_94_out, nand_95_out);
  nand nand_107 (c, nand_96_out, nand_97_out, nand_98_out, nand_99_out);
  nand nand_108 (d, nand_100_out, nand_101_out, nand_102_out, nand_103_out, nand_104_out);
endmodule
