// Logisim project display.circ as structural Verilog
module Decoder (
  input  A,
  input  B
);

  // AND_Gate BD is placed but not wired
  // AND_Gate B_D is placed but not wired
  // AND_Gate minus_B_D is placed but not wired
  // AND_Gate CD is placed but not wired
  // AND_Gate C_D is placed but not wired
  // AND_Gate minus_C_D is placed but not wired
  // AND_Gate B_CD is placed but not wired
  // AND_Gate B_C is placed but not wired
  // AND_Gate minus_BC is placed but not wired
  // AND_Gate minus_B_C is placed but not wired
endmodule
